# Fritzing sketch Breadboard Layout (saved by Fritzing 0.9.5d)
breadboards: 1

parts:
  Part1 = Arduino Nano (Rev3.0)
  M1 = DHT11-Grove-Temperature-Sensor_1

nets:
  N1: Part1.GND, M1.connector3
  N2: Part1.D4, M1.connector0
  N3: Part1.5V, M1.connector2
