# Fritzing sketch Breadboard Layout (saved by Fritzing 0.9.5d)
breadboards: 1

parts:
  Part1 = Arduino Nano (Rev3.0)
  J1 = Piezo Speaker
  ZS-042_RTC1 = ZS-042 RTC Module

nets:
  GND: Part1.GND, J1.pin1, ZS-042_RTC1.GND
  N1: Part1.D3, J1.pin2
  5V: Part1.5V, ZS-042_RTC1.VCC
  N2: Part1.A5, ZS-042_RTC1.SCL
  N3: Part1.A4, ZS-042_RTC1.SDA
