# Fritzing sketch Breadboard Layout (saved by Fritzing 0.9.5d)
breadboards: 1

parts:
  Part1 = Arduino Nano (Rev3.0)
  J1 = Piezo Speaker
  M1 = MAX30102

nets:
  GND: Part1.GND, J1.pin1, M1.GND
  N1: Part1.D3, J1.pin2
  5V: Part1.5V, M1.VIN
  N2: Part1.A5, M1.SCL
  N3: Part1.A4, M1.SDA

custom parts:
  MAX30102: Oximeter module using the MAX30102 chip. You may wish to read (and check your module) this post on power problems with these modules: https://reedpaper.wordpress.com/2018/08/22/pulse-oximeter-max30100-max30102-how-to-fix-wrong-board/ . As usual, if you want the mounting holes in pcb, you need to drag a hole over the pad in silkscreen to actually drill the hole (by default they are not drilled)
