# Fritzing sketch Breadboard Layout (saved by Fritzing 0.9.5d)
breadboards: 1

parts:
  Part1 = Arduino Nano (Rev3.0)
  Part2 = InvenSense MPU6050
  J1 = Piezo Speaker

nets:
  GND: Part1.GND, Part2.GND, J1.pin1
  N1: Part1.D3, J1.pin2
  5V: Part1.5V, Part2.VCC
  N2: Part1.A5, Part2.SCL
  N3: Part1.A4, Part2.SDA
